# Fritzing sketch LCD 16X2_AVR (saved by Fritzing 0.9.2b)

parts:
  Explore_AVR_Breakout_Board1 = Explore AVR Breakout Board  # not connected
  LCD1 = LCD screen  # not connected
  U1 = Explore Ultra One Board [package=THT]

nets:
  N1: U1.pin_96, U1.pin_198
  N2: U1.pin_97, U1.pin_199
  N3: U1.pin_98, U1.pin_200
  N4: U1.pin_99, U1.pin_201
  N5: U1.pin_154, U1.pin_189
  N6: U1.pin_155, U1.pin_190
  N7: U1.pin_156, U1.pin_191
